// Logisim project pli.circ as structural Verilog: 1 circuit, main circuit main
module main (
  input  REQ,
  input  RESET,
  output ENA,
  output STB,
  output ACK,
  output LAT
);

  wire and_1_out, CLK_out, d_ff_1_q, d_ff_2_q, d_ff_4_q, d_ff_4_qn, nor_2_out, not_1_out, or_1_out;

  Clock CLK (.out(CLK_out));
  not not_1 (not_1_out, CLK_out);
  D_Flip_Flop #(.trigger("high")) d_ff_1 (.clk(CLK_out), .D(REQ), .Q(d_ff_1_q));  // open: Qn, preset, en, reset
  D_Flip_Flop #(.trigger("high")) d_ff_2 (.clk(CLK_out), .D(or_1_out), .Q(d_ff_2_q));  // open: Qn, preset, en, reset
  or or_1 (or_1_out, STB, RESET);
  and and_1 (and_1_out, not_1_out, d_ff_2_q);
  nor nor_1 (LAT, d_ff_1_q, nor_2_out);
  nor nor_2 (nor_2_out, LAT, and_1_out);
  D_Flip_Flop #(.trigger("high")) d_ff_3 (.clk(not_1_out), .D(LAT), .Q(ENA));  // open: Qn, preset, en, reset
  D_Flip_Flop #(.trigger("high")) d_ff_4 (
    .clk(CLK_out), .D(ENA), .Q(d_ff_4_q), .Qn(d_ff_4_qn));  // open: preset, en, reset
  nor nor_3 (STB, d_ff_4_q, LAT);
  nor nor_4 (ACK, LAT, d_ff_4_qn);
endmodule
