// Logisim project sel02i.circ as structural Verilog: 1 circuit, main circuit main
module main (
  input  RESET,
  input  ACK,
  input  SEL02,
  output IRQ,
  output RPLY_S2,
  output SEL_OUT02
);

  wire CLK_out, d_ff_1_q, d_ff_3_qn, d_ff_4_q, nor_2_out, not_1_out, or_1_out;

  Clock CLK (.out(CLK_out));
  not not_1 (not_1_out, CLK_out);
  or or_1 (or_1_out, RESET, ACK);
  D_Flip_Flop #(.trigger("high")) d_ff_1 (.clk(CLK_out), .D(SEL_OUT02), .Q(d_ff_1_q));  // open: Qn, preset, en, reset
  and and_1 (SEL_OUT02, SEL02, d_ff_4_q);
  nor nor_1 (IRQ, or_1_out, nor_2_out);
  nor nor_2 (nor_2_out, IRQ, d_ff_1_q);
  D_Flip_Flop #(.trigger("high")) d_ff_2 (.clk(not_1_out), .D(nor_2_out), .Qn(RPLY_S2));  // open: Q, preset, en, reset
  D_Flip_Flop #(.trigger("high")) d_ff_3 (.clk(CLK_out), .D(RPLY_S2), .Qn(d_ff_3_qn));  // open: Q, preset, en, reset
  D_Flip_Flop #(.trigger("high")) d_ff_4 (.clk(not_1_out), .D(d_ff_3_qn), .Q(d_ff_4_q));  // open: Qn, preset, en, reset
endmodule
