// Logisim project uplr.circ as structural Verilog: 1 circuit, main circuit main
module main (
  input  REQ,
  input  RESET,
  input  ACK,
  output ENA,
  output REQ0,
  output REQ1
);

  wire CLK_out, d_ff_1_qn, d_ff_2_q, d_ff_3_q, nor_1_out, nor_2_out, nor_5_out, nor_6_out, nor_7_out,
       nor_8_out, not_1_out, not_2_out, or_1_out;

  Clock CLK (.out(CLK_out));
  not not_1 (not_1_out, REQ);
  not not_2 (not_2_out, ACK);
  or or_1 (or_1_out, RESET, nor_6_out);
  nor nor_1 (nor_1_out, d_ff_2_q, not_1_out);
  D_Flip_Flop #(.trigger("high")) d_ff_1 (.clk(CLK_out), .D(not_2_out), .Qn(d_ff_1_qn));  // open: Q, preset, en, reset
  nor nor_2 (nor_2_out, REQ, REQ0);
  nor nor_3 (REQ0, nor_2_out, or_1_out);
  nor nor_4 (REQ1, d_ff_1_qn, nor_5_out);
  nor nor_5 (nor_5_out, REQ1, nor_1_out);
  D_Flip_Flop #(.trigger("high")) d_ff_2 (.clk(not_1_out), .D(nor_2_out), .Q(d_ff_2_q));  // open: Qn, preset, en, reset
  D_Flip_Flop #(.trigger("high")) d_ff_3 (.clk(not_1_out), .D(REQ0), .Q(d_ff_3_q));  // open: Qn, preset, en, reset
  nor nor_6 (nor_6_out, d_ff_1_qn, REQ1, not_2_out);
  nor nor_7 (nor_7_out, not_1_out, d_ff_3_q);
  nor nor_8 (nor_8_out, d_ff_1_qn, nor_5_out, not_2_out);
  or or_2 (ENA, nor_7_out, nor_8_out);
endmodule
